// Logisim project StickyStacky16.circ as structural Verilog: 1 circuit, main circuit main
module main (
  input  [15:0] Input,
  input  [1:0] SPsel,
  input  [1:0] Wsel,
  input  Clock,
  output [15:0] stack_sp,
  output [15:0] stack_sp_2
);

  wire and_5_out, not_1_out, not_2_out, or_1_out, sp_nop, sp_pop, sp_push, sp_reset;
  wire [3:0] sp, sp_1, sp_1_t;
  wire [15:0] r0, r1, r2, r3, r4, r5, r6, r7, r8, r9, r10, r11, r12, r13, r14, r15, undriven;

  not not_1 (not_1_out, SPsel[0]);
  not not_2 (not_2_out, SPsel[1]);
  and and_1 (sp_push, SPsel[1], SPsel[0]);
  Register #(.width(16)) register_1 (.Q(r0), .clk(Clock));  // open: D, en, clr
  and and_2 (sp_nop, SPsel[1], not_1_out);
  Register #(.width(16)) register_2 (.D(undriven), .Q(r1), .clk(Clock));  // open: en, clr
  and and_3 (sp_reset, not_2_out, not_1_out);
  and and_4 (sp_pop, not_2_out, SPsel[0]);
  Register #(.width(16)) register_3 (.Q(r2), .clk(Clock));  // open: D, en, clr
  Register #(.width(16)) register_4 (.Q(r3), .clk(Clock));  // open: D, en, clr
  Multiplexer #(.select(4), .width(16)) multiplexer_1 (
    .in0(r0), .in1(r1), .in2(r2), .in3(r3), .in4(r4), .in5(r5), .in6(r6), .in7(r7), .in8(r8), .in9(r9),
    .in10(r10), .in11(r11), .in12(r12), .in13(r13), .in14(r14), .in15(r15), .out(stack_sp), .sel(sp));  // open: en
  Register #(.width(16)) register_5 (.Q(r4), .clk(Clock));  // open: D, en, clr
  Register #(.width(16)) register_6 (.Q(r5), .clk(Clock));  // open: D, en, clr
  Counter #(.width(4), .max('hf)) u_SP (
    .load(sp_push), .count(or_1_out), .Q(sp), .clk(Clock), .clr(and_5_out));  // open: D, carry
  or or_1 (or_1_out, sp_push, sp_pop);
  and and_5 (and_5_out, Clock, sp_reset);
  Register #(.width(16)) register_7 (.Q(r7), .clk(Clock));  // open: D, en, clr
  Register #(.width(16)) register_8 (.Q(r6), .clk(Clock));  // open: D, en, clr
  Multiplexer #(.select(4), .width(16)) multiplexer_2 (
    .in0(r0), .in1(r1), .in2(r2), .in3(r3), .in4(r4), .in5(r5), .in6(r6), .in7(r7), .in8(r8), .in9(r9),
    .in10(r10), .in11(r11), .in12(r12), .in13(r13), .in14(r14), .in15(r15), .out(stack_sp_2), .sel(sp_1));  // open: en
  Register #(.width(16)) register_9 (.Q(r8), .clk(Clock));  // open: D, en, clr
  // Probe on sp_1
  Adder #(.width(4)) adder_1 (.a(4'b0001), .b(sp), .out(sp_1));  // open: cin, cout
  // Probe on sp
  Subtractor #(.width(4)) subtractor_1 (.a(sp), .b(4'b0001), .out(sp_1_t));  // open: bin, bout
  // Probe on sp_1_t
  Register #(.width(16)) register_10 (.Q(r9), .clk(Clock));  // open: D, en, clr
  Register #(.width(16)) register_11 (.Q(r11), .clk(Clock));  // open: D, en, clr
  Register #(.width(16)) register_12 (.Q(r10), .clk(Clock));  // open: D, en, clr
  Register #(.width(16)) register_13 (.Q(r12), .clk(Clock));  // open: D, en, clr
  Register #(.width(16)) register_14 (.Q(r13), .clk(Clock));  // open: D, en, clr
  Register #(.width(16)) register_15 (.Q(r15), .clk(Clock));  // open: D, en, clr
  Register #(.width(16)) register_16 (.Q(r14), .clk(Clock));  // open: D, en, clr

  // Other names for the same wires on the sheet: spcell[1:0] = SPsel
endmodule
